# Fritzing sketch Volumio_Wemos_Rpi (saved by Fritzing 0.9.3b)

parts:
  Raspberry_Pi_1 = Raspberry Pi 3 [part_number=RPI-3-V1.2]
  WeMos_D1_Mini1 = WeMos D1 Mini

nets:
  N1: Raspberry_Pi_1.GPIO3, WeMos_D1_Mini1.D7
  N2: Raspberry_Pi_1.GPIO17, WeMos_D1_Mini1.D1
  N3: Raspberry_Pi_1.GPIO22, WeMos_D1_Mini1.D3
  N4: Raspberry_Pi_1.GPIO26, WeMos_D1_Mini1.D6
  N5: Raspberry_Pi_1.GPIO24, WeMos_D1_Mini1.D5
  N6: Raspberry_Pi_1.GPIO23, WeMos_D1_Mini1.D4
  N7: Raspberry_Pi_1.GPIO18, WeMos_D1_Mini1.D2
  N8: Raspberry_Pi_1.GND, WeMos_D1_Mini1.G
  5V: Raspberry_Pi_1.5V, WeMos_D1_Mini1.5V
